# Fritzing sketch 12_Lab-02 (saved by Fritzing 0.9.3b)
breadboards: 1

parts:
  WeMos_D1_Mini1 = WeMos D1 Mini
  LED1 = smd LED [color="Red (633nm)" package="0603 [SMD]"]
  LED2 = smd LED [color="Yellow (585nm)" package="0603 [SMD]"]
  LED3 = smd LED [color="Green (555nm)" package="0603 [SMD]"]
  R1 = Resistor [tolerance=±5% resistance=220 package=THT]

nets:
  N1: WeMos_D1_Mini1.3V3, LED2.anode, LED3.anode, R1.Pin_1
  N2: WeMos_D1_Mini1.D1, LED1.cathode
  N3: WeMos_D1_Mini1.D2, LED2.cathode
  N4: WeMos_D1_Mini1.D3, LED3.cathode
  N5: LED1.anode, R1.Pin_0
