# Fritzing sketch 22_Lab-02 (saved by Fritzing 0.9.3b)
breadboards: 1

parts:
  WeMos_D1_Mini1 = WeMos D1 Mini
  S1 = Pushbutton [package="[THT]"]
  S2 = Pushbutton [package="[THT]"]
  R1 = Resistor [tolerance=±5% resistance=220 package=THT]
  R2 = Resistor [tolerance=±5% resistance=220 package=THT]

nets:
  N1: WeMos_D1_Mini1.3V3, S2.Pin_1, S2.Pin_2, R1.Pin_1
  N2: WeMos_D1_Mini1.D1, S1.Pin_1, S1.Pin_2, R1.Pin_0
  N3: WeMos_D1_Mini1.D2, S2.Pin_3, S2.Pin_4, R2.Pin_0
  N4: WeMos_D1_Mini1.G, S1.Pin_3, S1.Pin_4, R2.Pin_1
