# Fritzing sketch 22_Lab-03 (saved by Fritzing 0.9.3b)
breadboards: 1

parts:
  WeMos_D1_Mini1 = WeMos D1 Mini
  S2 = Pushbutton [package="[THT]"]
  R1 = Resistor [tolerance=±5% resistance=220 package=THT]
  LED1 = LED - 5mm [color="Red (633nm)" package="5 mm [THT]"]
  R2 = Resistor [tolerance=±5% resistance=220 package=THT]

nets:
  N1: WeMos_D1_Mini1.3V3, S2.Pin_1, S2.Pin_2
  N2: WeMos_D1_Mini1.D1, R2.Pin_0
  N3: WeMos_D1_Mini1.D2, S2.Pin_3, S2.Pin_4, R1.Pin_0
  N4: WeMos_D1_Mini1.G, R1.Pin_1, LED1.cathode
  N5: LED1.anode, R2.Pin_1
