# Fritzing sketch 22_Lab-06 (saved by Fritzing 0.9.3b)
breadboards: 1

parts:
  WeMos_D1_Mini1 = WeMos D1 Mini
  J1 = Piezo Speaker

nets:
  N1: WeMos_D1_Mini1.D0, J1.pin2
  N2: WeMos_D1_Mini1.G, J1.pin1
